// Logisim project vrc6_cells.circ as structural Verilog: 9 circuits, main circuit vrc6_31aoi
module vrc6_31aoi (
  input  a0,
  input  a1,
  input  b0,
  input  b1,
  output x
);

  wire transistor_1_out, transistor_5_out, transistor_7_out;

  Transistor transistor_1 (.in(1'b1), .out(transistor_1_out), .gate(a0));
  Transistor transistor_2 (.in(1'b1), .out(transistor_1_out), .gate(a1));
  Transistor transistor_3 (.in(transistor_1_out), .out(x), .gate(b0));
  Transistor transistor_4 (.in(transistor_1_out), .out(x), .gate(b1));
  Transistor #(.\type ("n")) transistor_5 (.in(1'b0), .out(transistor_5_out), .gate(a0));
  Transistor #(.\type ("n")) transistor_6 (.in(transistor_5_out), .out(x), .gate(a1));
  Transistor #(.\type ("n")) transistor_7 (.in(1'b0), .out(transistor_7_out), .gate(b0));
  Transistor #(.\type ("n")) transistor_8 (.in(transistor_7_out), .out(x), .gate(b1));
endmodule

module mux2 (
  input  s0,
  input  s1,
  input  a0,
  input  a1,
  input  a2,
  input  a3,
  output x
);

  wire nand_1_out, nand_2_out, nand_3_out, nand_4_out, not_1_out, not_2_out, not_3_out, not_4_out;

  not not_1 (not_1_out, s0);
  not not_2 (not_2_out, s1);
  not not_3 (not_3_out, not_1_out);
  not not_4 (not_4_out, not_2_out);
  nand nand_1 (nand_1_out, a0, not_1_out, not_2_out);
  nand nand_2 (nand_2_out, a1, not_3_out, not_2_out);
  nand nand_3 (nand_3_out, a2, not_1_out, not_4_out);
  nand nand_4 (nand_4_out, a3, not_3_out, not_4_out);
  nand nand_5 (x, nand_1_out, nand_2_out, nand_3_out, nand_4_out);

  // Notes on the sheet:
  //   k1
  //   k2
  //   k3
  //   k4
  //   t1
  //   t2
  //   t3
  //   t4
endmodule

module vrc6_xor (
  input  a,
  input  b,
  output x
);

  wire nand_1_out, nand_2_out, or_1_out;

  nand nand_1 (nand_1_out, a, b);
  or or_1 (or_1_out, a, b);
  nand nand_2 (nand_2_out, or_1_out, nand_1_out);
  not not_1 (x, nand_2_out);
endmodule

module dec2 (
  input  n_ena,
  input  a1,
  input  a0,
  output nx0,
  output nx1,
  output nx2,
  output nx3
);

  wire not_1_out, not_2_out, not_3_out, not_4_out, not_5_out;

  not not_1 (not_1_out, n_ena);
  not not_2 (not_2_out, a1);
  not not_3 (not_3_out, a0);
  not not_4 (not_4_out, not_2_out);
  not not_5 (not_5_out, not_3_out);
  nand nand_1 (nx0, not_1_out, not_3_out, not_2_out);
  nand nand_2 (nx1, not_1_out, not_5_out, not_2_out);
  nand nand_3 (nx2, not_1_out, not_3_out, not_4_out);
  nand nand_4 (nx3, not_1_out, not_5_out, not_4_out);

  // Notes on the sheet:
  //   k1
  //   k4
  //   k5
  //   k2
  //   k3
endmodule

module dec4 (
  input  a4,
  input  a3,
  input  a2,
  input  a1,
  input  bin,
  output x4,
  output x3,
  output x2,
  output x1,
  output bout
);

  wire and_1_out, and_2_out, and_3_out, nand_1_out, nand_2_out, nand_3_out, nor_1_out, nor_2_out, nor_3_out,
       nor_4_out, nor_5_out, nor_6_out, nor_7_out, or_1_out;

  nand nand_1 (nand_1_out, nand_3_out, a4);
  or or_1 (or_1_out, nand_3_out, a4);
  and and_1 (and_1_out, a3, nor_2_out);
  nor nor_1 (nor_1_out, a3, nor_2_out);
  nor nor_2 (nor_2_out, nand_3_out, a4);
  nor nor_3 (nor_3_out, a4, a3, nand_3_out);
  and and_2 (and_2_out, nor_3_out, a2);
  nor nor_4 (nor_4_out, nor_3_out, a2);
  nor nor_5 (nor_5_out, a2, a3, a4, nand_3_out);
  nor nor_6 (nor_6_out, a1, a2, a3, a4);
  nor nor_7 (nor_7_out, a1, nor_5_out);
  and and_3 (and_3_out, a1, nor_5_out);
  not not_1 (bout, nand_2_out);
  nand nand_2 (nand_2_out, nor_6_out, bin);
  nand nand_3 (nand_3_out, bin, bin);
  nand nand_4 (x4, or_1_out, nand_1_out);
  nor nor_8 (x3, and_1_out, nor_1_out);
  nor nor_9 (x2, and_2_out, nor_4_out);
  nor nor_10 (x1, and_3_out, nor_7_out);

  // Notes on the sheet:
  //   lsb
  //   msb
  //   k1
  //   k1
  //   k4
  //   k3
  //   k3
  //   k2
  //   k1
  //   k1
  //   k1
  //   k4
  //   k3
  //   k2
  //   k1
  //   lsb
  //   msb
endmodule

module dec4_opt (
  input  in_1,
  input  in_2,
  input  a4,
  input  a3,
  input  a2,
  input  a1,
  input  in_7,
  input  in_8,
  input  bin,
  output x4,
  output out_11,
  output x3,
  output x2,
  output out_14,
  output x1,
  output bout
);

  wire and_2_out, nand_1_out, nor_1_out, nor_2_out, nor_3_out, nor_4_out, nor_6_out, not_1_out, or_1_out,
       xnor_2_out, xor_4_out;

  not not_1 (not_1_out, bin);
  nor nor_1 (nor_1_out, not_1_out, a4);
  nor nor_2 (nor_2_out, a4, a3, not_1_out);
  nor nor_3 (nor_3_out, a2, a3, a4, not_1_out);
  nor nor_4 (nor_4_out, a1, a2, a3, a4);
  xnor xnor_1 (x4, not_1_out, a4);
  and and_1 (bout, nor_4_out, bin);
  xor xor_1 (x3, a3, nor_1_out);
  xor xor_2 (x2, nor_2_out, a2);
  xor xor_3 (x1, a1, nor_3_out);
  or or_1 (or_1_out, in_1, in_2);
  and and_2 (and_2_out, in_7, in_8);
  nor nor_5 (out_14, and_2_out, nor_6_out);
  nor nor_6 (nor_6_out, in_7, in_8);
  nand nand_1 (nand_1_out, in_1, in_2);
  nand nand_2 (out_11, or_1_out, nand_1_out);
  xor xor_4 (xor_4_out, in_7, in_8);
  xnor xnor_2 (xnor_2_out, in_1, in_2);

  // Notes on the sheet:
  //   k1
  //   k1
  //   k1
  //   k1
  //   k1
  //   k1
  //   k1
  //   = 
  //   =
endmodule

module regbit (
  input  sel,
  input  clk,
  input  nd0,
  input  d1,
  input  sel_2,
  input  d0,
  input  d1_2,
  output q,
  output nq
);

  wire multiplexer_1_out, multiplexer_2_out, multiplexer_3_out, nand_1_out, nand_2_out, nand_3_out,
       nand_4_out, not_1_out, not_2_out, not_3_out, not_4_out, not_5_out, not_6_out, not_7_out, or_1_out,
       or_2_out;

  not not_1 (not_1_out, sel);
  not not_2 (not_2_out, sel_2);
  nand nand_1 (nand_1_out, not_1_out, nd0);
  nand nand_2 (nand_2_out, not_2_out, d0);
  not not_3 (not_3_out, d1_2);
  or or_1 (or_1_out, not_1_out, d1);
  or or_2 (or_2_out, not_2_out, d1_2);
  Multiplexer multiplexer_1 (.in0(d0), .in1(not_3_out), .out(multiplexer_1_out), .sel(sel_2));
  nand nand_3 (nand_3_out, or_1_out, nand_1_out);
  nand nand_4 (nand_4_out, or_2_out, nand_2_out);
  Multiplexer multiplexer_2 (.in0(nand_3_out), .in1(not_4_out), .out(multiplexer_2_out), .sel(clk));
  not not_4 (not_4_out, not_5_out);
  not not_5 (not_5_out, multiplexer_2_out);
  Multiplexer multiplexer_3 (.in0(not_6_out), .in1(not_5_out), .out(multiplexer_3_out), .sel(clk));
  not not_6 (not_6_out, not_7_out);
  not not_7 (not_7_out, multiplexer_3_out);
  not not_8 (q, not_7_out);
  not not_9 (nq, multiplexer_3_out);

  // Notes on the sheet:
  //   k1
  //   k1
  //   =
  //   ~d
  //   ~d
  //   ~d
  //   master
  //   w3
  //   slave
endmodule

module reg4 (
  input  sel,
  input  clk,
  input  [3:0] nd,
  input  [3:0] d,
  output [3:0] q,
  output [3:0] nq
);

  regbit regbit_1 (.sel(sel), .clk(clk), .nd0(nd[0]), .d1(d[0]), .q(q[0]), .nq(nq[0]));  // open: sel_2, d0, d1_2
  regbit regbit_2 (.sel(sel), .clk(clk), .nd0(nd[1]), .d1(d[1]), .q(q[1]), .nq(nq[1]));  // open: sel_2, d0, d1_2
  regbit regbit_3 (.sel(sel), .clk(clk), .nd0(nd[2]), .d1(d[2]), .q(q[2]), .nq(nq[2]));  // open: sel_2, d0, d1_2
  regbit regbit_4 (.sel(sel), .clk(clk), .nd0(nd[3]), .d1(d[3]), .q(q[3]), .nq(nq[3]));  // open: sel_2, d0, d1_2
endmodule

module latchbit (
  input  clk,
  input  d,
  output q
);

  wire multiplexer_1_out, not_1_out, not_2_out, not_3_out;

  not not_1 (not_1_out, d);
  Multiplexer multiplexer_1 (.in0(not_3_out), .in1(not_1_out), .out(multiplexer_1_out), .sel(clk));
  not not_2 (not_2_out, multiplexer_1_out);
  not not_3 (not_3_out, not_2_out);
  not not_4 (q, not_3_out);
endmodule
