// Logisim project MMC1A Logisim 2.7.1.circ as structural Verilog: 1 circuit, main circuit main
module main (
  input  M2,
  input  nROMSEL,
  input  CPU_A13,
  input  CPU_A14,
  input  CPU_RnW,
  input  CPU_D7,
  input  PPU_A11,
  input  PPU_A10,
  input  PPU_A12,
  input  CPU_D0,
  output SRAM_CE,
  output PRG__CE,
  output PRG_A17,
  output PRG_A16,
  output PRG_A15,
  output PRG_A14,
  output CIRAM_A10,
  output CHR_A12,
  output CHR_A13,
  output CHR_A14,
  output CHR_A15,
  output CHR_A16
);

  wire _11_out, _14_out, _15_out, _19_out, _20_out, _22_out, _25_out, _35_out, _48_out, _49_out, _50_out,
       _55_out, _56_out, _57_out, _66_out, _70_2_out, _70_out, _71_2_out, _71_out, _72_2_out, _72_out,
       _73_2_out, _73_out, _74_2_out, _74_out, _75_out, _85_2_out, _85_3_out, _85_out, _86_2_out, _86_3_out,
       _86_out, _87_out, _89_2_out, _89_3_out, _89_out, _105_2_out, _105_3_out, _105_out, _122_out, _123_out,
       _124_2_out, _124_out, _127_out, _131_2_out, _131_out, _132_2_out, _132_out, _135_2_out, _135_out,
       _136_2_out, _136_out, buffer_1_out, buffer_2_out, buffer_3_out, buffer_4_out, buffer_5_out,
       buffer_6_out, buffer_7_out, buffer_8_out, buffer_9_out, buffer_10_out, buffer_11_out, buffer_12_out,
       buffer_13_out, buffer_14_out, buffer_15_out, buffer_16_out, buffer_17_out, buffer_18_out,
       buffer_19_out, buffer_20_out, buffer_21_out, buffer_22_out, buffer_23_out, buffer_24_out,
       buffer_25_out, buffer_26_out, buffer_27_out, buffer_28_out, buffer_29_out, buffer_30_out,
       buffer_31_out, buffer_32_out, buffer_33_out, buffer_34_out, buffer_35_out, buffer_36_out,
       buffer_37_out, buffer_38_out, buffer_39_out, buffer_40_out, buffer_41_out, buffer_42_out,
       buffer_43_out, buffer_44_out, buffer_45_out, buffer_46_out, buffer_47_out, buffer_48_out,
       buffer_49_out, buffer_50_out, buffer_51_out, buffer_52_out, buffer_53_out, buffer_54_out, D_Latch_2_q,
       D_Latch_3_q, D_Latch_4_q, D_Latch_5_q, D_Latch_6_q, D_Latch_7_q, D_Latch_8_q, D_Latch_9_q,
       D_Latch_10_q, D_Latch_11_q, D_Latch_12_q, D_Latch_13_q, D_Latch_14_q, D_Latch_15_q, D_Latch_16_q,
       D_Latch_17_q, D_Latch_18_q, D_Latch_q, DFF_2_q, DFF_3_q, DFF_4_q, DFF_5_q, DFF_6_q, DFF_7_q, DFF_8_q,
       DFF_q, DFFNQ_2_q, DFFNQ_2_qn, DFFNQ_3_q, DFFNQ_3_qn, DFFNQ_4_q, DFFNQ_4_qn, DFFNQ_5_q, DFFNQ_5_qn,
       DFFNQ_6_q, DFFNQ_q, DFFNQ_qn, DFFRE_2_q, DFFRE_q, not_1_out, not_2_out, not_3_out, not_4_out,
       not_5_out, not_6_out, not_7_out, not_8_out, not_9_out, not_10_out, not_11_out, not_12_out, not_13_out,
       not_14_out, not_15_out, not_16_out, not_17_out, not_18_out, not_19_out, not_20_out, not_21_out,
       not_22_out, not_23_out;

  not not_1 (not_1_out, M2);
  buf buffer_1 (buffer_1_out, not_2_out);
  not not_2 (not_2_out, not_1_out);
  buf buffer_2 (buffer_2_out, not_1_out);
  not _22 (_22_out, CPU_D7);
  buf buffer_3 (buffer_3_out, buffer_4_out);
  buf buffer_4 (buffer_4_out, buffer_1_out);
  buf buffer_5 (buffer_5_out, buffer_2_out);
  nor _25 (_25_out, CPU_RnW, buffer_14_out);
  or _20 (_20_out, buffer_14_out, CPU_RnW, _22_out);
  buf buffer_6 (buffer_6_out, buffer_3_out);
  buf buffer_7 (buffer_7_out, buffer_6_out);
  D_Flip_Flop DFF (.clk(buffer_5_out), .D(_25_out), .Q(DFF_q));  // open: Qn, preset, en, reset
  D_Flip_Flop DFF_2 (.clk(not_2_out), .D(_20_out), .Q(DFF_2_q));  // open: Qn, preset, en, reset
  not not_3 (not_3_out, buffer_7_out);
  nand _87 (_87_out, DFF_q, not_3_out);
  not not_4 (not_4_out, _87_out);
  not not_5 (not_5_out, not_4_out);
  not not_6 (not_6_out, _87_out);
  not not_7 (not_7_out, not_5_out);
  not not_8 (not_8_out, not_6_out);
  not not_9 (not_9_out, not_7_out);
  not not_10 (not_10_out, not_8_out);
  not not_11 (not_11_out, not_9_out);
  D_Flip_Flop DFFNQ (.clk(not_11_out), .D(CPU_A14), .Q(DFFNQ_q), .Qn(DFFNQ_qn));  // open: preset, en, reset
  D_Flip_Flop DFFNQ_2 (.clk(not_11_out), .D(CPU_A13), .Q(DFFNQ_2_q), .Qn(DFFNQ_2_qn));  // open: preset, en, reset
  D_Flip_Flop DFFNQ_3 (
    .clk(not_11_out), .D(DFFNQ_3_qn), .Q(DFFNQ_3_q), .Qn(DFFNQ_3_qn), .reset(not_13_out));  // open: preset, en
  D_Flip_Flop DFFNQ_4 (
    .clk(DFFNQ_3_q), .D(DFFNQ_4_qn), .Q(DFFNQ_4_q), .Qn(DFFNQ_4_qn), .reset(not_13_out));  // open: preset, en
  D_Flip_Flop DFFNQ_5 (
    .clk(DFFNQ_4_q), .D(DFFNQ_5_qn), .Q(DFFNQ_5_q), .Qn(DFFNQ_5_qn), .reset(not_13_out));  // open: preset, en
  D_Flip_Flop DFFNQ_6 (.D(buffer_24_out), .Q(DFFNQ_6_q), .reset(not_12_out));  // open: clk, Qn, preset, en
  not not_12 (not_12_out, DFF_2_q);
  buf buffer_8 (buffer_8_out, buffer_7_out);
  buf buffer_9 (buffer_9_out, buffer_8_out);
  buf buffer_10 (buffer_10_out, buffer_18_out);
  buf buffer_11 (buffer_11_out, buffer_10_out);
  buf buffer_12 (buffer_12_out, buffer_11_out);
  buf buffer_13 (buffer_13_out, buffer_12_out);
  buf buffer_14 (buffer_14_out, buffer_15_out);
  buf buffer_15 (buffer_15_out, buffer_23_out);
  not not_13 (not_13_out, DFFNQ_6_q);
  buf buffer_16 (buffer_16_out, buffer_17_out);
  buf buffer_17 (buffer_17_out, buffer_9_out);
  buf buffer_18 (buffer_18_out, buffer_19_out);
  buf buffer_19 (buffer_19_out, buffer_27_out);
  buf buffer_20 (buffer_20_out, buffer_13_out);
  buf buffer_21 (buffer_21_out, buffer_20_out);
  buf buffer_22 (buffer_22_out, buffer_30_out);
  buf buffer_23 (buffer_23_out, buffer_22_out);
  nor _19 (_19_out, DFFNQ_qn, _15_out);
  nand _14 (_14_out, not_14_out, DFFNQ_2_qn);
  nand _15 (_15_out, DFFNQ_2_q, not_14_out);
  and _66 (_66_out, DFFNQ_3_q, DFFNQ_4_qn, DFFNQ_5_q);
  buf buffer_24 (buffer_24_out, _66_out);
  buf buffer_25 (buffer_25_out, buffer_16_out);
  buf buffer_26 (buffer_26_out, buffer_25_out);
  buf buffer_27 (buffer_27_out, buffer_28_out);
  buf buffer_28 (buffer_28_out, buffer_34_out);
  buf _35 (_35_out, buffer_29_out);
  buf buffer_29 (buffer_29_out, buffer_21_out);
  buf buffer_30 (buffer_30_out, nROMSEL);
  not not_14 (not_14_out, buffer_31_out);
  buf buffer_31 (buffer_31_out, buffer_24_out);
  buf buffer_32 (buffer_32_out, buffer_26_out);
  buf buffer_33 (buffer_33_out, buffer_32_out);
  buf buffer_34 (buffer_34_out, buffer_53_out);
  buf buffer_35 (buffer_35_out, buffer_36_out);
  buf buffer_36 (buffer_36_out, _35_out);
  not not_15 (not_15_out, _55_out);
  buf buffer_37 (buffer_37_out, _19_out);
  not not_16 (not_16_out, _19_out);
  nor _55 (_55_out, DFFNQ_q, _14_out);
  nor _56 (_56_out, _14_out, DFFNQ_qn);
  nor _57 (_57_out, _15_out, DFFNQ_q);
  D_Flip_Flop DFF_3 (.clk(not_11_out), .D(DFF_4_q), .Q(DFF_3_q));  // open: Qn, preset, en, reset
  D_Flip_Flop DFF_4 (.clk(not_11_out), .D(DFF_5_q), .Q(DFF_4_q));  // open: Qn, preset, en, reset
  D_Flip_Flop DFF_5 (.clk(not_11_out), .D(DFF_6_q), .Q(DFF_5_q));  // open: Qn, preset, en, reset
  D_Flip_Flop DFF_6 (.clk(not_11_out), .D(DFF_7_q), .Q(DFF_6_q));  // open: Qn, preset, en, reset
  D_Flip_Flop DFF_7 (.clk(not_11_out), .D(DFF_8_q), .Q(DFF_7_q));  // open: Qn, preset, en, reset
  D_Flip_Flop DFF_8 (.clk(buffer_5_out), .D(CPU_D0), .Q(DFF_8_q));  // open: Qn, preset, en, reset
  buf buffer_38 (buffer_38_out, buffer_33_out);
  buf buffer_39 (buffer_39_out, buffer_38_out);
  buf buffer_40 (buffer_40_out, buffer_41_out);
  buf buffer_41 (buffer_41_out, buffer_35_out);
  buf buffer_42 (buffer_42_out, buffer_43_out);
  buf buffer_43 (buffer_43_out, buffer_39_out);
  buf buffer_44 (buffer_44_out, buffer_45_out);
  buf buffer_45 (buffer_45_out, buffer_40_out);
  D_Flip_Flop #(.trigger("high")) D_Latch (
    .clk(buffer_37_out), .D(DFF_7_q), .Q(D_Latch_q));  // open: Qn, preset, en, reset
  D_Flip_Flop #(.trigger("high")) D_Latch_2 (
    .clk(buffer_37_out), .D(DFF_6_q), .Q(D_Latch_2_q));  // open: Qn, preset, en, reset
  D_Flip_Flop #(.trigger("high")) D_Latch_3 (
    .clk(buffer_37_out), .D(DFF_5_q), .Q(D_Latch_3_q));  // open: Qn, preset, en, reset
  D_Flip_Flop DFFRE (.clk(not_15_out), .D(DFF_6_q), .Q(DFFRE_q), .en(DFF_2_q));  // open: Qn, preset, reset
  D_Flip_Flop DFFRE_2 (.clk(not_15_out), .D(DFF_5_q), .Q(DFFRE_2_q), .en(DFF_2_q));  // open: Qn, preset, reset
  D_Flip_Flop #(.trigger("high")) D_Latch_4 (
    .clk(buffer_37_out), .D(DFF_4_q), .Q(D_Latch_4_q));  // open: Qn, preset, en, reset
  D_Flip_Flop #(.trigger("high")) D_Latch_5 (
    .clk(buffer_37_out), .D(DFF_3_q), .Q(D_Latch_5_q));  // open: Qn, preset, en, reset
  buf buffer_46 (buffer_46_out, _55_out);
  buf buffer_47 (buffer_47_out, _56_out);
  buf buffer_48 (buffer_48_out, _57_out);
  buf buffer_49 (buffer_49_out, buffer_42_out);
  buf buffer_50 (buffer_50_out, buffer_49_out);
  buf buffer_51 (buffer_51_out, buffer_52_out);
  buf buffer_52 (buffer_52_out, buffer_44_out);
  buf buffer_53 (buffer_53_out, buffer_50_out);
  buf buffer_54 (buffer_54_out, buffer_51_out);
  not not_17 (not_17_out, DFFRE_q);
  D_Flip_Flop #(.trigger("high")) D_Latch_6 (
    .clk(buffer_46_out), .D(DFF_3_q), .Q(D_Latch_6_q));  // open: Qn, preset, en, reset
  D_Flip_Flop #(.trigger("high")) D_Latch_7 (
    .clk(buffer_46_out), .D(DFF_4_q), .Q(D_Latch_7_q));  // open: Qn, preset, en, reset
  D_Flip_Flop #(.trigger("high")) D_Latch_8 (
    .clk(buffer_47_out), .D(DFF_3_q), .Q(D_Latch_8_q));  // open: Qn, preset, en, reset
  D_Flip_Flop #(.trigger("high")) D_Latch_9 (
    .clk(buffer_48_out), .D(DFF_3_q), .Q(D_Latch_9_q));  // open: Qn, preset, en, reset
  D_Flip_Flop #(.trigger("high")) D_Latch_10 (
    .clk(buffer_46_out), .D(DFF_7_q), .Q(D_Latch_10_q));  // open: Qn, preset, en, reset
  D_Flip_Flop #(.trigger("high")) D_Latch_11 (
    .clk(buffer_48_out), .D(DFF_4_q), .Q(D_Latch_11_q));  // open: Qn, preset, en, reset
  D_Flip_Flop #(.trigger("high")) D_Latch_12 (
    .clk(buffer_47_out), .D(DFF_4_q), .Q(D_Latch_12_q));  // open: Qn, preset, en, reset
  D_Flip_Flop #(.trigger("high")) D_Latch_13 (
    .clk(buffer_48_out), .D(DFF_5_q), .Q(D_Latch_13_q));  // open: Qn, preset, en, reset
  D_Flip_Flop #(.trigger("high")) D_Latch_14 (
    .clk(buffer_47_out), .D(DFF_5_q), .Q(D_Latch_14_q));  // open: Qn, preset, en, reset
  D_Flip_Flop #(.trigger("high")) D_Latch_15 (
    .clk(buffer_48_out), .D(DFF_6_q), .Q(D_Latch_15_q));  // open: Qn, preset, en, reset
  D_Flip_Flop #(.trigger("high")) D_Latch_16 (
    .clk(buffer_47_out), .D(DFF_6_q), .Q(D_Latch_16_q));  // open: Qn, preset, en, reset
  D_Flip_Flop #(.trigger("high")) D_Latch_17 (
    .clk(buffer_48_out), .D(DFF_7_q), .Q(D_Latch_17_q));  // open: Qn, preset, en, reset
  D_Flip_Flop #(.trigger("high")) D_Latch_18 (
    .clk(buffer_47_out), .D(DFF_7_q), .Q(D_Latch_18_q));  // open: Qn, preset, en, reset
  and _11 (_11_out, buffer_53_out, buffer_54_out);
  and _85 (_85_out, not_17_out, D_Latch_2_q);
  and _85_2 (_85_2_out, DFFRE_2_q, D_Latch_2_q);
  and _86 (_86_out, 1'b1, DFFRE_2_q, not_18_out);
  and _86_2 (_86_2_out, not_18_out, DFFRE_2_q, DFFRE_q);
  not not_18 (not_18_out, D_Latch_q);
  or _71 (_71_out, DFFRE_2_q, DFFRE_q);
  and _70 (_70_out, D_Latch_3_q, DFFRE_q);
  or _73 (_73_out, DFFRE_2_q, DFFRE_q);
  and _72 (_72_out, D_Latch_4_q, DFFRE_q);
  not not_19 (not_19_out, D_Latch_10_q);
  and _127 (_127_out, PPU_A12, D_Latch_10_q);
  or _85_3 (_85_3_out, _85_out, _85_2_out);
  or _86_3 (_86_3_out, _86_out, _86_2_out);
  and _71_2 (_71_2_out, _71_out, D_Latch_3_q);
  or _70_2 (_70_2_out, DFFRE_2_q, _70_out);
  and _73_2 (_73_2_out, D_Latch_4_q, _73_out);
  or _72_2 (_72_2_out, DFFRE_2_q, _72_out);
  or _75 (_75_out, not_17_out, DFFRE_2_q, D_Latch_5_q);
  not not_20 (not_20_out, D_Latch_6_q);
  not not_21 (not_21_out, D_Latch_7_q);
  or _122 (_122_out, D_Latch_8_q, not_19_out);
  not not_22 (not_22_out, PPU_A12);
  or _123 (_123_out, not_19_out, not_22_out);
  and _49 (_49_out, _11_out, nROMSEL, CPU_A13, CPU_A14);
  not not_23 (not_23_out, CPU_RnW);
  and _89 (_89_out, _85_3_out, not_18_out);
  and _89_2 (_89_2_out, _86_3_out, CPU_A14);
  and _89_3 (_89_3_out, D_Latch_2_q, D_Latch_q);
  and _48 (_48_out, _71_2_out, CPU_A14);
  and _50 (_50_out, _73_2_out, CPU_A14);
  and _74 (_74_out, CPU_A14, _75_out, 1'b1);
  and _74_2 (_74_2_out, DFFRE_2_q, DFFRE_q, D_Latch_5_q);
  and _105 (_105_out, PPU_A11, D_Latch_6_q, D_Latch_7_q);
  and _105_2 (_105_2_out, not_20_out, D_Latch_7_q, PPU_A10);
  and _105_3 (_105_3_out, D_Latch_6_q, not_21_out, 1'b1);
  and _124 (_124_out, 1'b1, _122_out, PPU_A12);
  and _124_2 (_124_2_out, not_22_out, D_Latch_9_q, D_Latch_10_q);
  and _135 (_135_out, _123_out, D_Latch_11_q);
  and _135_2 (_135_2_out, _127_out, D_Latch_12_q);
  and _131 (_131_out, _123_out, D_Latch_13_q);
  and _131_2 (_131_2_out, _127_out, D_Latch_14_q);
  and _132 (_132_out, _123_out, D_Latch_15_q);
  and _132_2 (_132_2_out, _127_out, D_Latch_16_q);
  and _136 (_136_out, _123_out, D_Latch_17_q);
  and _136_2 (_136_2_out, _127_out, D_Latch_18_q);
  and _2 (SRAM_CE, M2, _49_out);
  or _3 (PRG__CE, nROMSEL, not_23_out);
  or _89_4 (PRG_A17, _89_out, _89_2_out, _89_3_out);
  or _48_2 (PRG_A16, _48_out, _70_2_out);
  or _50_2 (PRG_A15, _50_out, _72_2_out);
  or _74_3 (PRG_A14, _74_out, _74_2_out);
  or _105_4 (CIRAM_A10, _105_out, _105_2_out, _105_3_out);
  or _124_3 (CHR_A12, _124_out, _124_2_out);
  or _135_3 (CHR_A13, _135_out, _135_2_out);
  or _131_3 (CHR_A14, _131_out, _131_2_out);
  or _132_3 (CHR_A15, _132_out, _132_2_out);
  or _136_3 (CHR_A16, _136_out, _136_2_out);

  // Notes on the sheet:
  //   1
  //   4
  //   51
  //   5
  //   114
  //   113
  //   5
  //   116
  //   140
  //   139
  //   26
  //   137
  //   103
  //   13
  //   138
  //   53
  //   54
  //   63
  //   64
  //   65
  //   52
  //   142
  //   141
  //   47
  //   46
  //   43
  //   45
  //   28
  //   29
  //   115
  //   111
  //   42
  //   44
  //   39
  //   41
  //   27
  //   24
  //   60
  //   110
  //   108
  //   38
  //   40
  //   37
  //   16
  //   17
  //   18
  //   107
  //   106
  //   36
  //   31
  //   34
  //   69
  //   58
  //   61
  //   92
  //   98
  //   99
  //   82
  //   81
  //   62
  //   109
  //   112
  //   12
  //   23
  //   117
  //   59
  //   6
  //   10
  //   84
  //   83
  //   78
  //   91
  //   90
  //   77
  //   76
  //   68
  //   118
  //   133
  //   32
  //   30
  //   8
  //   7
  //   100
  //   95
  //   79
  //   121
  //   128
  //   80
  //   101
  //   94
  //   129
  //   96
  //   130
  //   93
  //   102
  //   97
  //   33
  //   9
  //   67
  //   125
  //   21
  //   104
  //   88
  //   126
endmodule
