// Logisim project MMC1_logism.circ as structural Verilog: 4 circuits, main circuit Mirroring
module main (
  input  CA10,
  input  CA11,
  input  CA12,
  input  PD7,
  input  PD0,
  input  nROMSEL,
  input  R_W,
  input  PA13,
  input  PA14,
  input  PHI2,
  output CIRAM_A10,
  output CHRA12,
  output CHRA13,
  output CHRA14,
  output CHRA15,
  output CHRA16,
  output PRGA14,
  output PRGA15,
  output PRGA16,
  output PRGA17,
  output ROM_nCE,
  output SRAM_CE
);

  wire and_1_out, decoder_1_out0, decoder_1_out1, decoder_1_out2, decoder_1_out3, not_1_out, not_2_out,
       not_3_out, not_4_out, or_1_out, or_3_out, or_4_out;
  wire [2:0] counter_1_q;
  wire [3:0] d_ff_4_q;
  wire [4:0] multiplexer_1_out, or_5_out, Reg0__Status_q, Reg1__CHR_A_q, Reg2__CHR_B_q, Reg3__PRG_q;

  or or_1 (or_1_out, nROMSEL, R_W);
  not not_1 (not_1_out, R_W);
  and and_1 (and_1_out, PD7, not_2_out);
  not not_2 (not_2_out, or_1_out);
  or or_2 (ROM_nCE, nROMSEL, not_1_out);
  or or_3 (or_3_out, and_1_out, counter_1_q[2]);
  not not_3 (not_3_out, or_3_out);
  Counter #(.width(3), .max('h7)) counter_1 (
    .load(or_3_out), .D(3'b000), .count(not_3_out), .Q(counter_1_q), .clk(or_1_out));  // open: carry, clr
  D_Flip_Flop d_ff_1 (.clk(or_1_out), .D(PD0), .Q(d_ff_4_q[3]));  // open: Qn, preset, en, reset
  D_Flip_Flop d_ff_2 (.clk(or_1_out), .D(d_ff_4_q[2]), .Q(d_ff_4_q[1]));  // open: Qn, preset, en, reset
  D_Flip_Flop d_ff_3 (.clk(or_1_out), .D(d_ff_4_q[3]), .Q(d_ff_4_q[2]));  // open: Qn, preset, en, reset
  or or_4 (or_4_out, and_1_out, decoder_1_out0);
  D_Flip_Flop d_ff_4 (.clk(or_1_out), .D(d_ff_4_q[1]), .Q(d_ff_4_q[0]));  // open: Qn, preset, en, reset
  Decoder #(.select(2), .disabled(0)) decoder_1 (
    .out0(decoder_1_out0), .out1(decoder_1_out1), .out2(decoder_1_out2), .out3(decoder_1_out3),
    .sel({PA14, PA13}), .en(counter_1_q[2]));
  assign or_5_out = 5'b01100 | Reg0__Status_q;  // OR_Gate or_5, 5 bits wide
  Multiplexer #(.width(5), .enable("false")) multiplexer_1 (
    .in0({PD0, d_ff_4_q}), .in1(or_5_out), .out(multiplexer_1_out), .sel(and_1_out));
  Register #(.width(5)) Reg0__Status (
    .D(multiplexer_1_out), .en(or_4_out), .Q(Reg0__Status_q), .clk(or_1_out));  // open: clr
  Register #(.width(5)) Reg1__CHR_A (
    .D({PD0, d_ff_4_q}), .en(decoder_1_out1), .Q(Reg1__CHR_A_q), .clk(or_1_out));  // open: clr
  Register #(.width(5)) Reg2__CHR_B (
    .D({PD0, d_ff_4_q}), .en(decoder_1_out2), .Q(Reg2__CHR_B_q), .clk(or_1_out));  // open: clr
  Register #(.width(5)) Reg3__PRG (
    .D({PD0, d_ff_4_q}), .en(decoder_1_out3), .Q(Reg3__PRG_q), .clk(or_1_out));  // open: clr
  not not_4 (not_4_out, Reg3__PRG_q[4]);
  and and_2 (SRAM_CE, not_4_out, PA14, PA13, nROMSEL, PHI2);
  Mirroring mirroring_1 (
    .Mirror1(Reg0__Status_q[1]), .Mirror2(Reg0__Status_q[0]), .CHRA10(CA10), .CHRA11(CA11),
    .CIRAM_A10(CIRAM_A10));
  CHR_switch chr_switch_1 (
    .A0(Reg1__CHR_A_q[0]), .A1(Reg1__CHR_A_q[1]), .A2(Reg1__CHR_A_q[2]), .A3(Reg1__CHR_A_q[3]),
    .A4(Reg1__CHR_A_q[4]), .B0(Reg2__CHR_B_q[0]), .B1(Reg2__CHR_B_q[1]), .B2(Reg2__CHR_B_q[2]),
    .B3(Reg2__CHR_B_q[3]), .B4(Reg2__CHR_B_q[4]), .CHRA12(CHRA12), .CHRA13(CHRA13), .CHRA14(CHRA14),
    .CHRA15(CHRA15), .CHRA16(CHRA16), .CA12(CA12), .CHR_Mode(Reg0__Status_q[4]));
  PRG_switch prg_switch_1 (
    .PRG_Mode1(Reg0__Status_q[2]), .PRG_Mode2(Reg0__Status_q[3]), .PA14(PA14), .Q0(Reg3__PRG_q[0]),
    .Q1(Reg3__PRG_q[1]), .Q2(Reg3__PRG_q[2]), .Q3(Reg3__PRG_q[3]), .PRG_A14(PRGA14), .PRG_A15(PRGA15),
    .PRG_A16(PRGA16), .PRG_A17(PRGA17));

  // Notes on the sheet:
  //   <- Only in MMC1B rev
endmodule

module Mirroring (
  input  Mirror1,
  input  Mirror2,
  input  CHRA10,
  input  CHRA11,
  output CIRAM_A10
);

  wire and_1_out, and_2_out, and_3_out, not_1_out, not_2_out;

  not not_1 (not_1_out, Mirror1);
  and and_1 (and_1_out, not_1_out, Mirror2);
  and and_2 (and_2_out, Mirror2, CHRA11);
  and and_3 (and_3_out, Mirror1, not_2_out, CHRA10);
  not not_2 (not_2_out, Mirror2);
  or or_1 (CIRAM_A10, and_1_out, and_2_out, and_3_out);
endmodule

module PRG_switch (
  input  PRG_Mode1,
  input  PRG_Mode2,
  input  PA14,
  input  Q0,
  input  Q1,
  input  Q2,
  input  Q3,
  output PRG_A14,
  output PRG_A15,
  output PRG_A16,
  output PRG_A17
);

  wire and_1_out, and_2_out, and_3_out, and_4_out, and_5_out, and_6_out, and_7_out, and_8_out, and_9_out,
       and_10_out, and_11_out, and_12_out, and_13_out, and_14_out, and_15_out, and_16_out, not_1_out,
       not_2_out, not_3_out, not_4_out;

  not not_1 (not_1_out, PRG_Mode1);
  not not_2 (not_2_out, PRG_Mode1);
  not not_3 (not_3_out, PRG_Mode1);
  not not_4 (not_4_out, PRG_Mode1);
  and and_1 (and_1_out, not_1_out, PA14);
  and and_2 (and_2_out, PA14, Q0);
  and and_3 (and_3_out, PRG_Mode2, PA14);
  and and_4 (and_4_out, PRG_Mode1, PRG_Mode2, Q0);
  and and_5 (and_5_out, not_2_out, Q1);
  and and_6 (and_6_out, PA14, Q1);
  and and_7 (and_7_out, PRG_Mode2, Q1);
  and and_8 (and_8_out, PRG_Mode1, PRG_Mode2, PA14);
  and and_9 (and_9_out, not_3_out, Q2);
  and and_10 (and_10_out, PA14, Q2);
  and and_11 (and_11_out, PRG_Mode2, Q2);
  and and_12 (and_12_out, PRG_Mode1, PRG_Mode2, PA14);
  and and_13 (and_13_out, not_4_out, Q3);
  and and_14 (and_14_out, PA14, Q3);
  and and_15 (and_15_out, PRG_Mode2, Q3);
  and and_16 (and_16_out, PRG_Mode1, PRG_Mode2, PA14);
  or or_1 (PRG_A14, and_1_out, and_2_out, and_3_out, and_4_out);
  or or_2 (PRG_A15, and_5_out, and_6_out, and_7_out, and_8_out);
  or or_3 (PRG_A16, and_9_out, and_10_out, and_11_out, and_12_out);
  or or_4 (PRG_A17, and_13_out, and_14_out, and_15_out, and_16_out);
endmodule

module CHR_switch (
  input  A0,
  input  CHR_Mode,
  input  A1,
  input  CA12,
  input  A2,
  input  A3,
  input  A4,
  input  B0,
  input  B1,
  input  B2,
  input  B3,
  input  B4,
  output CHRA12,
  output CHRA13,
  output CHRA14,
  output CHRA15,
  output CHRA16
);

  wire [4:0] multiplexer_1_out;

  Multiplexer #(.width(5)) multiplexer_1 (
    .in0({A4, A3, A2, A1, A0}), .in1({B4, B3, B2, B1, B0}), .out(multiplexer_1_out), .sel(CA12));  // open: en
  Multiplexer #(.width(5)) multiplexer_2 (
    .in0({A4, A3, A2, A1, CA12}), .in1(multiplexer_1_out), .out({CHRA16, CHRA15, CHRA14, CHRA13, CHRA12}),
    .sel(CHR_Mode));  // open: en
endmodule
