// Logisim project mmc1.circ as structural Verilog: 8 circuits, main circuit dff
module dff (
  input  clk,
  input  d,
  output q
);

  wire multiplexer_1_out, multiplexer_2_out, not_1_out, not_2_out, not_3_out, not_4_out;

  Multiplexer multiplexer_1 (.in0(d), .in1(not_2_out), .out(multiplexer_1_out), .sel(clk));
  not not_1 (not_1_out, multiplexer_1_out);
  not not_2 (not_2_out, not_1_out);
  Multiplexer multiplexer_2 (.in0(not_3_out), .in1(not_1_out), .out(multiplexer_2_out), .sel(clk));
  not not_3 (not_3_out, not_4_out);
  not not_4 (not_4_out, multiplexer_2_out);
  not not_5 (q, multiplexer_2_out);

  // Notes on the sheet:
  //   master
  //   slave
endmodule

module aon (
  input  a0,
  input  a1,
  input  a2,
  input  b0,
  input  b1,
  input  b2,
  output x
);

  wire and_1_out, and_2_out, or_1_out, transistor_1_out, transistor_5_out, transistor_6_out,
       transistor_7_out, transistor_9_out, transistor_10_out, transistor_15_out;

  Transistor #(.\type ("n")) transistor_1 (.in(transistor_5_out), .out(transistor_1_out), .gate(a0));
  Transistor transistor_2 (.in(1'b1), .out(transistor_1_out), .gate(a0));
  Transistor transistor_3 (.in(1'b1), .out(transistor_1_out), .gate(a1));
  Transistor transistor_4 (.in(1'b1), .out(transistor_1_out), .gate(a2));
  Transistor #(.\type ("n")) transistor_5 (.in(transistor_6_out), .out(transistor_5_out), .gate(a1));
  Transistor #(.\type ("n")) transistor_6 (.in(1'b0), .out(transistor_6_out), .gate(a2));
  Transistor transistor_7 (.in(1'b1), .out(transistor_7_out), .gate(b0));
  Transistor transistor_8 (.in(1'b1), .out(transistor_7_out), .gate(b1));
  Transistor #(.\type ("n")) transistor_9 (.in(1'b0), .out(transistor_9_out), .gate(b0));
  Transistor #(.\type ("n")) transistor_10 (.in(transistor_9_out), .out(transistor_10_out), .gate(b1));
  Transistor transistor_11 (.in(1'b1), .out(transistor_7_out), .gate(b2));
  Transistor #(.\type ("n")) transistor_12 (.in(transistor_10_out), .out(transistor_7_out), .gate(b2));
  Transistor transistor_13 (.in(1'b1), .out(x), .gate(transistor_7_out));
  Transistor transistor_14 (.in(1'b1), .out(x), .gate(transistor_1_out));
  Transistor #(.\type ("n")) transistor_15 (.in(1'b0), .out(transistor_15_out), .gate(transistor_7_out));
  Transistor #(.\type ("n")) transistor_16 (.in(transistor_15_out), .out(x), .gate(transistor_1_out));
  and and_1 (and_1_out, a0, a1, a2);
  and and_2 (and_2_out, b0, b1, b2);
  or or_1 (or_1_out, and_1_out, and_2_out);

  // Notes on the sheet:
  //   tran
  //   33-AON
  //   "three+three and to or Non-inverting"
  //   logic
  //   x
endmodule

module dffr (
  input  clk,
  input  nres,
  input  d,
  output q
);

  wire multiplexer_1_out, multiplexer_2_out, nor_1_out, nor_2_out, not_1_out, not_2_out, not_3_out;

  nor nor_1 (nor_1_out, not_1_out, not_2_out);
  not not_1 (not_1_out, nres);
  not not_2 (not_2_out, multiplexer_1_out);
  Multiplexer multiplexer_1 (.in0(d), .in1(nor_1_out), .out(multiplexer_1_out), .sel(clk));
  Multiplexer multiplexer_2 (.in0(nor_2_out), .in1(nor_1_out), .out(multiplexer_2_out), .sel(clk));
  not not_3 (not_3_out, multiplexer_2_out);
  not not_4 (q, not_3_out);
  nor nor_2 (nor_2_out, not_1_out, not_3_out);

  // Notes on the sheet:
  //   Master
  //   async_res
  //   Slave
endmodule

module dffr_nq (
  input  clk,
  input  nres,
  input  d,
  output q,
  output nq
);

  wire multiplexer_1_out, multiplexer_2_out, nor_1_out, nor_2_out, not_1_out, not_2_out, not_3_out;

  nor nor_1 (nor_1_out, not_1_out, not_2_out);
  not not_1 (not_1_out, nres);
  not not_2 (not_2_out, multiplexer_1_out);
  Multiplexer multiplexer_1 (.in0(d), .in1(nor_1_out), .out(multiplexer_1_out), .sel(clk));
  Multiplexer multiplexer_2 (.in0(nor_2_out), .in1(nor_1_out), .out(multiplexer_2_out), .sel(clk));
  not not_3 (not_3_out, multiplexer_2_out);
  not not_4 (q, not_3_out);
  nor nor_2 (nor_2_out, not_1_out, not_3_out);
  not not_5 (nq, nor_2_out);

  // Notes on the sheet:
  //   Master
  //   async_res
  //   Slave
endmodule

module dffrs (
  input  clk,
  input  nres,
  input  nset1,
  input  nset2,
  input  d,
  output q
);

  wire and_1_out, and_2_out, multiplexer_1_out, multiplexer_2_out, nor_1_out, nor_2_out, not_1_out,
       not_2_out, not_3_out;

  and and_1 (and_1_out, nset1, not_2_out);
  nor nor_1 (nor_1_out, not_1_out, and_1_out);
  not not_1 (not_1_out, nres);
  not not_2 (not_2_out, multiplexer_1_out);
  Multiplexer multiplexer_1 (.in0(d), .in1(nor_1_out), .out(multiplexer_1_out), .sel(clk));
  Multiplexer multiplexer_2 (.in0(nor_2_out), .in1(nor_1_out), .out(multiplexer_2_out), .sel(clk));
  not not_3 (not_3_out, multiplexer_2_out);
  not not_4 (q, not_3_out);
  nor nor_2 (nor_2_out, not_1_out, and_2_out);
  and and_2 (and_2_out, nset2, not_3_out);

  // Notes on the sheet:
  //   Master
  //   nset1 = nset2 for most cases
  //   async_res
  //   Slave
endmodule

module oan (
  input  a0,
  input  a1,
  input  b,
  output x
);

  wire nand_1_out, or_1_out;

  or or_1 (or_1_out, a0, a1);
  nand nand_1 (nand_1_out, or_1_out, b);
  not not_1 (x, nand_1_out);
endmodule

module aon_1 (
  input  a0,
  input  a1,
  input  b,
  output x
);

  wire and_1_out, nor_1_out;

  and and_1 (and_1_out, a0, a1);
  nor nor_1 (nor_1_out, and_1_out, b);
  not not_1 (x, nor_1_out);
endmodule

module reg_decoder (
  input  A13,
  input  A14,
  input  n_enable,
  output Reg0_ena,
  output Reg2_ena,
  output Reg3_ena,
  output Reg1_ena
);

  wire g14_out, g15_out, not_1_out, not_2_out, not_3_out;

  not not_1 (not_1_out, A13);
  not not_2 (not_2_out, A14);
  not not_3 (not_3_out, n_enable);
  nand g14 (g14_out, not_1_out, not_3_out);
  nand g15 (g15_out, not_3_out, A13);
  nor g55 (Reg0_ena, g14_out, A14);
  nor g56 (Reg2_ena, g14_out, not_2_out);
  nor g19 (Reg3_ena, not_2_out, g15_out);
  nor g57 (Reg1_ena, g15_out, A14);

  // Notes on the sheet:
  //   ena
endmodule
